# Fritzing sketch Robot_Arm_esquema (saved by Fritzing 1.0.2b)

parts:
  Servo_base = Basic Servo
  Servo_hombro = Basic Servo
  Servo_codo = Basic Servo
  Servo_garra = Basic Servo
  VCC1 = Battery
  A1 = Adafruit v1.2 motor shield
  U1 = SWITCH-SPST-2 [package=switch-spst-vertical]
  Componente1 = Bluetooth HC-05 Macho

nets:
  GND: Servo_base.gnd, Servo_hombro.gnd, Servo_codo.gnd, Servo_garra.gnd, VCC1.-, A1.Pin_3, A1.Pin_7, A1.Pin_32, A1.Pin_33, A1.Pin_34, A1.Pin_35, A1.Pin_37, A1.Pin_46, Componente1.GND
  VCC: Servo_base.vcc, Servo_hombro.vcc, Servo_codo.vcc, Servo_garra.vcc, A1.Pin_38, A1.Pin_39, A1.Pin_40, A1.Pin_41, A1.Pin_42, A1.Pin_43, A1.Pin_69, Componente1.VCC
  N1: Servo_base.pulse, A1.Pin_60
  N2: Servo_hombro.pulse, A1.Pin_59, A1.Pin_68
  N3: Servo_codo.pulse, A1.Pin_58, A1.Pin_65
  N4: Servo_garra.pulse, A1.Pin_55
  N5: VCC1.+, U1.P
  N6: A1.Pin_6, U1.O
  N7: A1.Pin_49, Componente1.TXD
  N8: A1.Pin_50, Componente1.RXD

custom parts:
  Adafruit v1.2 motor shield: Adafruit v1.2 motor shield.
